// Logisim project Registrador de deslocamento.circ as structural Verilog: 1 circuit, main circuit main
module main (
  input  Clock,
  input  in_2,
  input  in_3,
  input  in_4,
  input  in_5,
  input  in_6,
  input  in_7,
  input  in_8,
  input  in_9,
  input  in_10,
  input  in_11
);

  wire Dado;
  wire [4:0] d_ff_10_q;
  wire [4:1] d_ff_7_q;

  // Probe on {d_ff_7_q, Dado}
  // Probe on {d_ff_7_q, Dado}
  // Probe on d_ff_10_q
  // Probe on d_ff_10_q
  D_Flip_Flop #(.trigger("falling")) d_ff_1 (
    .clk(Clock), .D(1'b0), .Q(d_ff_7_q[4]), .preset(in_2), .reset(in_3));  // open: Qn, en
  D_Flip_Flop d_ff_2 (.clk(Clock), .D(Dado), .Q(d_ff_10_q[4]));  // open: Qn, preset, en, reset
  D_Flip_Flop #(.trigger("falling")) d_ff_3 (
    .clk(Clock), .D(d_ff_7_q[4]), .Q(d_ff_7_q[3]), .preset(in_4), .reset(in_5));  // open: Qn, en
  D_Flip_Flop d_ff_4 (.clk(Clock), .D(d_ff_10_q[4]), .Q(d_ff_10_q[3]));  // open: Qn, preset, en, reset
  D_Flip_Flop #(.trigger("falling")) d_ff_5 (
    .clk(Clock), .D(d_ff_7_q[3]), .Q(d_ff_7_q[2]), .preset(in_6), .reset(in_7));  // open: Qn, en
  D_Flip_Flop d_ff_6 (.clk(Clock), .D(d_ff_10_q[3]), .Q(d_ff_10_q[2]));  // open: Qn, preset, en, reset
  D_Flip_Flop #(.trigger("falling")) d_ff_7 (
    .clk(Clock), .D(d_ff_7_q[2]), .Q(d_ff_7_q[1]), .preset(in_8), .reset(in_9));  // open: Qn, en
  D_Flip_Flop d_ff_8 (.clk(Clock), .D(d_ff_10_q[2]), .Q(d_ff_10_q[1]));  // open: Qn, preset, en, reset
  D_Flip_Flop #(.trigger("falling")) d_ff_9 (
    .clk(Clock), .D(d_ff_7_q[1]), .Q(Dado), .preset(in_10), .reset(in_11));  // open: Qn, en
  D_Flip_Flop d_ff_10 (.clk(Clock), .D(d_ff_10_q[1]), .Q(d_ff_10_q[0]));  // open: Qn, preset, en, reset

  // Notes on the sheet:
  //   Registrador de deslocamento
  //   Transmissor
  //   Receptor
endmodule
