// Logisim project ContadorASsincronoCrescenteDecrescenteFFJK.circ as structural Verilog: 1 circuit, main circuit main
module main (
  input  Clock,
  input  Clock_2
);

  wire j_k_ff_1_qn, j_k_ff_3_qn, j_k_ff_5_qn;
  wire [3:0] j_k_ff_1_q, j_k_ff_2_q;

  // Probe on j_k_ff_1_q
  // Probe on j_k_ff_1_q
  // Probe on j_k_ff_1_q
  // Probe on j_k_ff_1_q
  // Probe on j_k_ff_2_q
  // Probe on j_k_ff_2_q
  // Probe on j_k_ff_2_q
  // Probe on j_k_ff_2_q
  J_K_Flip_Flop j_k_ff_1 (
    .J(Clock), .clk(Clock), .K(Clock), .Q(j_k_ff_1_q[0]), .Qn(j_k_ff_1_qn));  // open: preset, en, reset
  J_K_Flip_Flop j_k_ff_2 (.J(Clock_2), .clk(Clock_2), .K(Clock_2), .Q(j_k_ff_2_q[0]));  // open: Qn, preset, en, reset
  J_K_Flip_Flop j_k_ff_3 (
    .J(j_k_ff_1_qn), .clk(j_k_ff_1_qn), .K(j_k_ff_1_qn), .Q(j_k_ff_1_q[1]), .Qn(j_k_ff_3_qn));  // open: preset, en, reset
  J_K_Flip_Flop j_k_ff_4 (
    .J(j_k_ff_2_q[0]), .clk(j_k_ff_2_q[0]), .K(j_k_ff_2_q[0]), .Q(j_k_ff_2_q[1]));  // open: Qn, preset, en, reset
  J_K_Flip_Flop j_k_ff_5 (
    .J(j_k_ff_3_qn), .clk(j_k_ff_3_qn), .K(j_k_ff_3_qn), .Q(j_k_ff_1_q[2]), .Qn(j_k_ff_5_qn));  // open: preset, en, reset
  J_K_Flip_Flop j_k_ff_6 (
    .J(j_k_ff_2_q[1]), .clk(j_k_ff_2_q[1]), .K(j_k_ff_2_q[1]), .Q(j_k_ff_2_q[2]));  // open: Qn, preset, en, reset
  J_K_Flip_Flop j_k_ff_7 (
    .J(j_k_ff_5_qn), .clk(j_k_ff_5_qn), .K(j_k_ff_5_qn), .Q(j_k_ff_1_q[3]));  // open: Qn, preset, en, reset
  J_K_Flip_Flop j_k_ff_8 (
    .J(j_k_ff_2_q[2]), .clk(j_k_ff_2_q[2]), .K(j_k_ff_2_q[2]), .Q(j_k_ff_2_q[3]));  // open: Qn, preset, en, reset

  // Notes on the sheet:
  //   0 a 15
  //   0 a 15
  //   Contador Assíncrono Crescente FF JK
  //   Contador Assíncrono Crescente FF JK
endmodule
