// Logisim project ContadorAssincronoCrescenteDecrescenteFFT.circ as structural Verilog: 1 circuit, main circuit main
module main (
  input  Clock,
  input  Clock_2
);

  wire t_ff_1_qn, t_ff_3_qn, t_ff_5_qn;
  wire [3:0] t_ff_1_q, t_ff_2_q;

  // Probe on t_ff_1_q
  // Probe on t_ff_1_q
  // Probe on t_ff_1_q
  // Probe on t_ff_1_q
  T_Flip_Flop t_ff_1 (.clk(Clock), .T(Clock), .Q(t_ff_1_q[0]), .Qn(t_ff_1_qn));  // open: preset, reset, en
  // Probe on t_ff_2_q
  // Probe on t_ff_2_q
  // Probe on t_ff_2_q
  // Probe on t_ff_2_q
  T_Flip_Flop t_ff_2 (.clk(Clock_2), .T(Clock_2), .Q(t_ff_2_q[0]));  // open: Qn, preset, reset, en
  T_Flip_Flop t_ff_3 (.clk(t_ff_1_qn), .T(t_ff_1_qn), .Q(t_ff_1_q[1]), .Qn(t_ff_3_qn));  // open: preset, reset, en
  T_Flip_Flop t_ff_4 (.clk(t_ff_2_q[0]), .T(t_ff_2_q[0]), .Q(t_ff_2_q[1]));  // open: Qn, preset, reset, en
  T_Flip_Flop t_ff_5 (.clk(t_ff_3_qn), .T(t_ff_3_qn), .Q(t_ff_1_q[2]), .Qn(t_ff_5_qn));  // open: preset, reset, en
  T_Flip_Flop t_ff_6 (.clk(t_ff_2_q[1]), .T(t_ff_2_q[1]), .Q(t_ff_2_q[2]));  // open: Qn, preset, reset, en
  T_Flip_Flop t_ff_7 (.clk(t_ff_5_qn), .T(t_ff_5_qn), .Q(t_ff_1_q[3]));  // open: Qn, preset, reset, en
  T_Flip_Flop t_ff_8 (.clk(t_ff_2_q[2]), .T(t_ff_2_q[2]), .Q(t_ff_2_q[3]));  // open: Qn, preset, reset, en

  // Notes on the sheet:
  //   0 a 15
  //   0 a 15
  //   Contador Assíncrono Crescente FF T
  //   Contador Assíncrono Decrescente FF T
endmodule
