// Logisim project ContadorAssincronoCrescenteDescrescente0a15.circ as structural Verilog: 1 circuit, main circuit main
module main (
  input  Clock,
  input  Clock_2
);

  wire d_ff_1_qn, d_ff_2_qn, d_ff_3_qn, d_ff_4_qn, LSB_2_qn, LSB_qn, MSB_2_qn, MSB_qn;
  wire [3:0] LSB_2_q, LSB_q;

  // Probe on LSB_q
  // Probe on LSB_q
  // Probe on LSB_q
  // Probe on LSB_q
  D_Flip_Flop LSB (.clk(Clock), .D(LSB_qn), .Q(LSB_q[0]), .Qn(LSB_qn));  // open: preset, en, reset
  // Probe on LSB_2_q
  // Probe on LSB_2_q
  // Probe on LSB_2_q
  // Probe on LSB_2_q
  D_Flip_Flop LSB_2 (.clk(Clock_2), .D(LSB_2_qn), .Q(LSB_2_q[0]), .Qn(LSB_2_qn));  // open: preset, en, reset
  D_Flip_Flop d_ff_1 (.clk(LSB_2_q[0]), .D(d_ff_1_qn), .Q(LSB_2_q[1]), .Qn(d_ff_1_qn));  // open: preset, en, reset
  D_Flip_Flop d_ff_2 (.clk(LSB_qn), .D(d_ff_2_qn), .Q(LSB_q[1]), .Qn(d_ff_2_qn));  // open: preset, en, reset
  D_Flip_Flop d_ff_3 (.clk(d_ff_2_qn), .D(d_ff_3_qn), .Q(LSB_q[2]), .Qn(d_ff_3_qn));  // open: preset, en, reset
  D_Flip_Flop d_ff_4 (.clk(LSB_2_q[1]), .D(d_ff_4_qn), .Q(LSB_2_q[2]), .Qn(d_ff_4_qn));  // open: preset, en, reset
  D_Flip_Flop MSB (.clk(d_ff_3_qn), .D(MSB_qn), .Q(LSB_q[3]), .Qn(MSB_qn));  // open: preset, en, reset
  D_Flip_Flop MSB_2 (.clk(LSB_2_q[2]), .D(MSB_2_qn), .Q(LSB_2_q[3]), .Qn(MSB_2_qn));  // open: preset, en, reset

  // Notes on the sheet:
  //   0 a 15
  //   15 a 0
  //   Contador Assíncrono Crescente
  //   Contador Assíncrono Decrescente
endmodule
