// Logisim project ShiftRegisterJK5bits.circ as structural Verilog: 1 circuit, main circuit main
module main (
  input  in_1,
  input  in_2,
  input  in_3,
  input  in_4,
  input  in_5,
  input  in_6,
  input  in_7,
  input  in_8,
  input  in_9,
  input  in_10
);

  wire Clock2, Dado2, j_k_ff_1_qn, j_k_ff_2_qn, j_k_ff_3_qn, j_k_ff_4_qn, j_k_ff_5_qn, j_k_ff_6_qn,
       j_k_ff_7_qn, j_k_ff_8_qn, not_1_out, not_2_out;
  wire [4:0] j_k_ff_10_q;
  wire [4:1] j_k_ff_7_q;

  // Probe on {j_k_ff_7_q, Dado2}
  // Probe on {j_k_ff_7_q, Dado2}
  Clock clock_1 (.out(Clock2));
  not not_1 (not_1_out, 1'b0);
  // Probe on j_k_ff_10_q
  // Probe on j_k_ff_10_q
  J_K_Flip_Flop j_k_ff_1 (
    .J(1'b0), .clk(Clock2), .K(not_1_out), .Q(j_k_ff_7_q[4]), .Qn(j_k_ff_1_qn), .preset(in_1), .reset(in_2));  // open: en
  J_K_Flip_Flop j_k_ff_2 (
    .J(Dado2), .clk(Clock2), .K(not_2_out), .Q(j_k_ff_10_q[4]), .Qn(j_k_ff_2_qn));  // open: preset, en, reset
  not not_2 (not_2_out, Dado2);
  J_K_Flip_Flop j_k_ff_3 (
    .J(j_k_ff_7_q[4]), .clk(Clock2), .K(j_k_ff_1_qn), .Q(j_k_ff_7_q[3]), .Qn(j_k_ff_3_qn), .preset(in_3),
    .reset(in_4));  // open: en
  J_K_Flip_Flop j_k_ff_4 (
    .J(j_k_ff_10_q[4]), .clk(Clock2), .K(j_k_ff_2_qn), .Q(j_k_ff_10_q[3]), .Qn(j_k_ff_4_qn));  // open: preset, en, reset
  J_K_Flip_Flop j_k_ff_5 (
    .J(j_k_ff_7_q[3]), .clk(Clock2), .K(j_k_ff_3_qn), .Q(j_k_ff_7_q[2]), .Qn(j_k_ff_5_qn), .preset(in_5),
    .reset(in_6));  // open: en
  J_K_Flip_Flop j_k_ff_6 (
    .J(j_k_ff_10_q[3]), .clk(Clock2), .K(j_k_ff_4_qn), .Q(j_k_ff_10_q[2]), .Qn(j_k_ff_6_qn));  // open: preset, en, reset
  J_K_Flip_Flop j_k_ff_7 (
    .J(j_k_ff_7_q[2]), .clk(Clock2), .K(j_k_ff_5_qn), .Q(j_k_ff_7_q[1]), .Qn(j_k_ff_7_qn), .preset(in_7),
    .reset(in_8));  // open: en
  J_K_Flip_Flop j_k_ff_8 (
    .J(j_k_ff_10_q[2]), .clk(Clock2), .K(j_k_ff_6_qn), .Q(j_k_ff_10_q[1]), .Qn(j_k_ff_8_qn));  // open: preset, en, reset
  J_K_Flip_Flop j_k_ff_9 (
    .J(j_k_ff_7_q[1]), .clk(Clock2), .K(j_k_ff_7_qn), .Q(Dado2), .preset(in_9), .reset(in_10));  // open: Qn, en
  J_K_Flip_Flop j_k_ff_10 (
    .J(j_k_ff_10_q[1]), .clk(Clock2), .K(j_k_ff_8_qn), .Q(j_k_ff_10_q[0]));  // open: Qn, preset, en, reset

  // Notes on the sheet:
  //   Registrador de deslocamento jk
  //   Transmissor
  //   Receptor
endmodule
