// Logisim project TodosContadoresFlipFLop.circ as structural Verilog: 1 circuit, main circuit main
module main (
  input  Clock,
  input  Clock_2,
  input  Clock_3,
  input  Clock_4,
  input  Clock_5,
  input  Clock_6
);

  wire d_ff_1_qn, d_ff_2_qn, d_ff_3_qn, d_ff_4_qn, j_k_ff_1_qn, j_k_ff_4_qn, j_k_ff_5_qn, LSB_2_qn, LSB_qn,
       MSB_2_qn, MSB_qn, t_ff_1_qn, t_ff_3_qn, t_ff_5_qn;
  wire [3:0] j_k_ff_1_q, j_k_ff_2_q, LSB_2_q, LSB_q, t_ff_1_q, t_ff_2_q;

  // Probe on LSB_q
  // Probe on LSB_q
  // Probe on LSB_q
  // Probe on LSB_q
  D_Flip_Flop LSB (.clk(Clock_3), .D(LSB_qn), .Q(LSB_q[0]), .Qn(LSB_qn));  // open: preset, en, reset
  // Probe on LSB_2_q
  // Probe on LSB_2_q
  // Probe on LSB_2_q
  // Probe on LSB_2_q
  D_Flip_Flop LSB_2 (.clk(Clock_5), .D(LSB_2_qn), .Q(LSB_2_q[0]), .Qn(LSB_2_qn));  // open: preset, en, reset
  D_Flip_Flop d_ff_1 (.clk(LSB_2_q[0]), .D(d_ff_1_qn), .Q(LSB_2_q[1]), .Qn(d_ff_1_qn));  // open: preset, en, reset
  D_Flip_Flop d_ff_2 (.clk(LSB_qn), .D(d_ff_2_qn), .Q(LSB_q[1]), .Qn(d_ff_2_qn));  // open: preset, en, reset
  D_Flip_Flop d_ff_3 (.clk(d_ff_2_qn), .D(d_ff_3_qn), .Q(LSB_q[2]), .Qn(d_ff_3_qn));  // open: preset, en, reset
  D_Flip_Flop d_ff_4 (.clk(LSB_2_q[1]), .D(d_ff_4_qn), .Q(LSB_2_q[2]), .Qn(d_ff_4_qn));  // open: preset, en, reset
  D_Flip_Flop MSB (.clk(d_ff_3_qn), .D(MSB_qn), .Q(LSB_q[3]), .Qn(MSB_qn));  // open: preset, en, reset
  D_Flip_Flop MSB_2 (.clk(LSB_2_q[2]), .D(MSB_2_qn), .Q(LSB_2_q[3]), .Qn(MSB_2_qn));  // open: preset, en, reset
  // Probe on t_ff_1_q
  // Probe on t_ff_1_q
  // Probe on t_ff_1_q
  // Probe on t_ff_1_q
  T_Flip_Flop t_ff_1 (.clk(Clock), .T(Clock), .Q(t_ff_1_q[0]), .Qn(t_ff_1_qn));  // open: preset, reset, en
  // Probe on t_ff_2_q
  // Probe on t_ff_2_q
  // Probe on t_ff_2_q
  // Probe on t_ff_2_q
  T_Flip_Flop t_ff_2 (.clk(Clock_4), .T(Clock_4), .Q(t_ff_2_q[0]));  // open: Qn, preset, reset, en
  T_Flip_Flop t_ff_3 (.clk(t_ff_1_qn), .T(t_ff_1_qn), .Q(t_ff_1_q[1]), .Qn(t_ff_3_qn));  // open: preset, reset, en
  T_Flip_Flop t_ff_4 (.clk(t_ff_2_q[0]), .T(t_ff_2_q[0]), .Q(t_ff_2_q[1]));  // open: Qn, preset, reset, en
  T_Flip_Flop t_ff_5 (.clk(t_ff_3_qn), .T(t_ff_3_qn), .Q(t_ff_1_q[2]), .Qn(t_ff_5_qn));  // open: preset, reset, en
  T_Flip_Flop t_ff_6 (.clk(t_ff_2_q[1]), .T(t_ff_2_q[1]), .Q(t_ff_2_q[2]));  // open: Qn, preset, reset, en
  T_Flip_Flop t_ff_7 (.clk(t_ff_5_qn), .T(t_ff_5_qn), .Q(t_ff_1_q[3]));  // open: Qn, preset, reset, en
  T_Flip_Flop t_ff_8 (.clk(t_ff_2_q[2]), .T(t_ff_2_q[2]), .Q(t_ff_2_q[3]));  // open: Qn, preset, reset, en
  // Probe on j_k_ff_1_q
  // Probe on j_k_ff_1_q
  // Probe on j_k_ff_1_q
  // Probe on j_k_ff_1_q
  J_K_Flip_Flop j_k_ff_1 (
    .J(Clock_2), .clk(Clock_2), .K(Clock_2), .Q(j_k_ff_1_q[0]), .Qn(j_k_ff_1_qn));  // open: preset, en, reset
  // Probe on j_k_ff_2_q
  // Probe on j_k_ff_2_q
  // Probe on j_k_ff_2_q
  // Probe on j_k_ff_2_q
  J_K_Flip_Flop j_k_ff_2 (.J(Clock_6), .clk(Clock_6), .K(Clock_6), .Q(j_k_ff_2_q[0]));  // open: Qn, preset, en, reset
  J_K_Flip_Flop j_k_ff_3 (
    .J(j_k_ff_2_q[0]), .clk(j_k_ff_2_q[0]), .K(j_k_ff_2_q[0]), .Q(j_k_ff_2_q[1]));  // open: Qn, preset, en, reset
  J_K_Flip_Flop j_k_ff_4 (
    .J(j_k_ff_1_qn), .clk(j_k_ff_1_qn), .K(j_k_ff_1_qn), .Q(j_k_ff_1_q[1]), .Qn(j_k_ff_4_qn));  // open: preset, en, reset
  J_K_Flip_Flop j_k_ff_5 (
    .J(j_k_ff_4_qn), .clk(j_k_ff_4_qn), .K(j_k_ff_4_qn), .Q(j_k_ff_1_q[2]), .Qn(j_k_ff_5_qn));  // open: preset, en, reset
  J_K_Flip_Flop j_k_ff_6 (
    .J(j_k_ff_2_q[1]), .clk(j_k_ff_2_q[1]), .K(j_k_ff_2_q[1]), .Q(j_k_ff_2_q[2]));  // open: Qn, preset, en, reset
  J_K_Flip_Flop j_k_ff_7 (
    .J(j_k_ff_5_qn), .clk(j_k_ff_5_qn), .K(j_k_ff_5_qn), .Q(j_k_ff_1_q[3]));  // open: Qn, preset, en, reset
  J_K_Flip_Flop j_k_ff_8 (
    .J(j_k_ff_2_q[2]), .clk(j_k_ff_2_q[2]), .K(j_k_ff_2_q[2]), .Q(j_k_ff_2_q[3]));  // open: Qn, preset, en, reset

  // Notes on the sheet:
  //   0 a 15
  //   15 a 0
  //   Contador Assíncrono Crescente
  //   Contador Assíncrono Decrescente
  //   0 a 15
  //   0 a 15
  //   Contador Assíncrono Crescente FF T
  //   Contador Assíncrono Decrescente FF T
  //   0 a 15
  //   0 a 15
  //   Contador Assíncrono Crescente FF JK
  //   Contador Assíncrono Crescente FF JK
endmodule
